# Fritzing sketch Wav File Player (saved by Fritzing 0.9.4)
breadboards: 1

parts:
  S1 = SWITCH-MOMENTARY-2 [package=tactile-pth]
  S2 = SWITCH-MOMENTARY-2 [package=tactile-pth]
  S3 = SWITCH-MOMENTARY-2 [package=tactile-pth]
  S4 = SWITCH-MOMENTARY-2 [package=tactile-pth]
  S5 = SWITCH-MOMENTARY-2 [package=tactile-pth]
  S6 = SWITCH-MOMENTARY-2 [package=tactile-pth]
  S7 = SWITCH-MOMENTARY-2 [package=tactile-pth]  # not connected
  U1 = 2.5mm Audio Jack [package=stereojack2.5mm_specia_pogopins]
  U2 = LCD-16X2 [package=lcd-16x2]
  microSD1 = MicroSD Card Module
  U3 = atmega328 [package=dip]
  U4 = LM386 [package=dip08]
  Y1 = CRYSTAL [package=hc49u-v]
  C1 = Capacitor [package=cap-pth-small2]
  R1 = TRIMPOT [package=trimpot-5mm]
  U5 = LIPO-1000mAh [package=lipo-1000]
  C2 = Capacitor [package=cap-pth-small2]

nets:
  N1: S1.1, U3.A5
  GND: S1.2, S2.2, S3.2, S4.2, S5.2, S6.2, U1.SLEEVE, U2.VSS, U2.K, microSD1.GND, U3.GND, U4.-IN, U4.V-, R1.CCW, U5.-
  N2: S2.1, U3.A4
  N3: S3.1, U3.A3
  N4: S4.1, U3.A2
  N5: S5.1, U3.A1
  N6: S6.1, U3.A0
  N7: U1.LEFT, U1.RIGHT, C1.2
  VCC: U2.VDD, U2.E, U2.A, microSD1.VCC, U3.VCC, U3.AVCC, U3.AREF, U4.V+, R1.CW, U5.+
  N8: U2.VO, R1.WIPER
  N9: U2.DB0, U3.D7
  N10: U2.DB1, U3.D8
  N11: U2.DB2, U3.D9_(PWM)
  N12: U2.DB3, U3.D10_(PWM)
  N13: microSD1.MISO, U3.D12
  N14: microSD1.MOSI, U3.D11_(PWM)
  N15: microSD1.SCK, U3.D13
  N16: microSD1.CS, U3.D2
  N17: U3.D3_(PWM), U4.+IN
  N18: U3.XLAT1, Y1.1
  N19: U3.XLAT2, Y1.2
  N20: U4.GAIN, C2.1, C2.2
  N21: U4.OUT, C1.1
